# Fritzing sketch Motor Control (saved by Fritzing 0.9.6b)
breadboards: 1

parts:
  Mod1 = Raspberry Pi Pico
  L293D_H-Bridge = EDGY [part_number=www.rkeducation.co.uk]
  Motor = DC Motor
  Test_Button = Momentary Switch [package=ksa_sealed_tac_switch]
  FTDI_USB-TTL = FTDI Basic Programmer
  U1 = POT [package=pot_alpha_rv16af-20]

nets:
  N1: Mod1.pin_1, FTDI_USB-TTL.RXI
  N2: Mod1.pin_2, FTDI_USB-TTL.TXO
  GND: Mod1.pin_3, Mod1.pin_8, Mod1.pin_13, Mod1.pin_18, Mod1.pin_23, Mod1.pin_28, Mod1.pin_33, Mod1.pin_38, Mod1.pin_42, L293D_H-Bridge.GND, Test_Button.2, FTDI_USB-TTL.GND, U1.A
  N3: Mod1.pin_17, L293D_H-Bridge.A1
  N4: Mod1.pin_19, L293D_H-Bridge.Speed1
  N5: Mod1.pin_20, L293D_H-Bridge.B1
  N6: Mod1.pin_21, Test_Button.3
  N7: Mod1.pin_31, U1.S
  N8: Mod1.pin_36, U1.E
  N9: L293D_H-Bridge.B1out, Motor.pin_2
  N10: L293D_H-Bridge.A1out, Motor.pin_1

notes:
  PC Motor Control Demo
  RGP - 2021
  PC USB connection
  USB Program / debug

custom parts:
  Raspberry Pi Pico: Raspberry Pi Pico. Based around the RP2040 microcontroller the Pico is a low cost microcontroller device bringing Raspberry Pi quality, cost, and easy of use to the microcontroller space. Jan 2021, Split part in to two versions: tht (this one) and SMD. This one will drill holes for a .1 in header in pcb to allow plugging in the module as well as providing pads to solder the module to the top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
